# Fritzing sketch diagramaGeneral (saved by Fritzing 0.9.3b)
breadboards: 1

parts:
  U1 = NodeMCU V3.0
  Componente1 = Adafruit CCS811 [part_number="Adafruit #3566"]  # not connected
  LED1 = RGB LED (com. cathode, rgb) [package="5 mm [THT]"]

nets:
  N1: U1.GND#6, U1.GND#13, U1.GND#16, U1.GND#33, LED1.common_cathode
  N2: U1.D5, LED1.red_anode
  N3: U1.D6, LED1.green_anode
  N4: U1.D7, LED1.blue_anode

custom parts:
  NodeMCU V3.0: ESP8266 based NodeMCU
  Adafruit CCS811: Breathe easy - we finally have an I2C VOC/eCO2 sensor in the Adafruit shop! Add air quality monitoring to your project and with an Adafruit CCS811 Air Quality Sensor Breakout. This sensor from AMS is a gas sensor that can detect a wide range of Volatile Organic Compounds (VOCs) and is intended for indoor air quality monitoring. When connected to your microcontroller (running our library code)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
